# Fritzing sketch PCB (saved by Fritzing 0.9.2b)
circuit board: 5cm x 5cm
breadboards: 1

parts:
  R1 = Resistor [tolerance=±5% resistance=220 package=THT]
  R2 = Basic Flex Resistor
  R3 = Basic Flex Resistor
  R4 = Basic Flex Resistor
  R5 = Basic Flex Resistor
  R6 = Basic Flex Resistor
  R7 = Basic Flex Resistor
  R8 = Basic Flex Resistor
  R9 = Basic Flex Resistor
  R10 = Resistor [tolerance=±5% resistance=220 package=THT]
  R11 = Resistor [tolerance=±5% resistance=220 package=THT]
  R12 = Resistor [tolerance=±5% resistance=220 package=THT]
  R13 = Resistor [tolerance=±5% resistance=220 package=THT]
  R14 = Resistor [tolerance=±5% resistance=220 package=THT]
  R15 = Resistor [tolerance=±5% resistance=220 package=THT]
  R16 = Resistor [tolerance=±5% resistance=220 package=THT]
  Q1 = PNP-Transistor [package="TO92 [THT]"]
  Q2 = PNP-Transistor [package="TO92 [THT]"]
  Q3 = PNP-Transistor [package="TO92 [THT]"]
  Q4 = PNP-Transistor [package="TO92 [THT]"]
  Q5 = PNP-Transistor [package="TO92 [THT]"]
  Q6 = PNP-Transistor [package="TO92 [THT]"]
  Q7 = PNP-Transistor [package="TO92 [THT]"]
  Q8 = PNP-Transistor [package="TO92 [THT]"]
  LED1 = LED - 5mm [color="Red (633nm)" package="5 mm [THT]"]
  R17 = Basic Flex Resistor
  J1 = female pin header, 2 pins [form="♀ (female)"]
  R18 = Basic Flex Resistor
  R19 = Basic Flex Resistor
  R20 = Basic Flex Resistor
  R21 = Basic Flex Resistor
  R22 = Basic Flex Resistor
  R23 = Basic Flex Resistor
  R24 = Basic Flex Resistor
  R25 = Basic Flex Resistor
  R26 = Basic Flex Resistor
  R27 = Basic Flex Resistor

nets:
  N1: R1.Pin_0, R2.pin_1, R21.pin_1
  N2: R1.Pin_1, Q1.C
  N3: R2.Pin_2, R3.Pin_2, R4.Pin_2, R5.Pin_2, R6.Pin_2, R7.Pin_2, R8.Pin_2, R9.Pin_2, Q1.E, Q2.E, Q3.E, Q4.E, Q5.E, Q6.E, Q7.E, Q8.E, R17.pin_1, J1.pin1, R22.Pin_2, R23.Pin_2
  N4: R3.pin_1, R10.Pin_0, R21.Pin_2
  N5: R4.pin_1, R11.Pin_0, R20.pin_1
  N6: R5.pin_1, R12.Pin_0, R20.Pin_2
  N7: R6.pin_1, R16.Pin_0, R18.Pin_2
  N8: R7.pin_1, R15.Pin_0, R18.pin_1
  N9: R8.pin_1, R14.Pin_0, R19.Pin_2
  N10: R9.pin_1, R13.Pin_0, R19.pin_1
  N11: R10.Pin_1, Q2.C
  N12: R11.Pin_1, Q3.C
  N13: R12.Pin_1, Q4.C
  N14: R13.Pin_1, Q5.C
  N15: R14.Pin_1, Q6.C
  N16: R15.Pin_1, Q7.C
  N17: R16.Pin_1, Q8.C
  N18: Q1.B, R24.pin_1
  N19: Q2.B, R24.Pin_2
  N20: Q3.B, R25.pin_1
  N21: Q4.B, R25.Pin_2
  N22: Q5.B, R26.pin_1
  N23: Q6.B, R26.Pin_2
  N24: Q7.B, R27.pin_1
  N25: Q8.B, R27.Pin_2
  N26: LED1.cathode, J1.pin2, R22.pin_1, R23.pin_1
  N27: LED1.anode, R17.Pin_2

notes:
  GND
  5v
  0  1  2  3  4  5  6  7
  GND VIN
  GND VCC
  © N. Whyte
